// Logisim project cpu.circ as structural Verilog: 10 circuits, main circuit main
// CPU
module main (
  input  [31:0] RS_READ_VALUE,
  input  [31:0] RI_READ_VALUE,
  input  [31:0] RD_READ_VALUE,
  input  [31:0] JC_READ_VALUE,
  input  [31:0] INSTRUCTION,
  input  CLOCK,
  output [4:0] RS,
  output [4:0] RI,
  output [4:0] RD,
  output [31:0] RD_WRITE_VALUE,
  output RD_WRITE_ENABLE,
  output [23:0] FETCH_ADDRESS
);

  wire and_1_out, and_3_out, and_4_out, bit_extender_1_out, bit_extender_12_out, bit_extender_13_out,
       comparator_1_lt, comparator_2_eq, comparator_3_eq, comparator_4_eq, comparator_5_eq, comparator_6_eq,
       comparator_7_eq, comparator_9_eq, comparator_11_eq, comparator_12_gt, comparator_14_lt, cond, Imm,
       j_0, j_0_t, j_0_t_t, jump, not_1_out, not_2_out, not_3_out, not_4_out, not_5_out, not_6_out,
       not_7_out, not_8_out, or_1_out, RD_WRITE_ENABLE_t, ZC;
  wire [2:0] JC;
  wire [3:0] ctrl_op, shifter_6_out;
  wire [4:0] demultiplexer_5_out1, RD1, RD2;
  wire [15:0] JVal;
  wire [16:0] ImmVal;
  wire [23:0] adder_1_out, adder_2_out, bit_extender_15_out, bit_extender_16_out, demultiplexer_2_out1,
       demultiplexer_3_out1, j_0out, j_0out_t, j_0out_t_t, j__0out, j__0out_t, j__0out_t_t, j__out, jfinal,
       multiplexer_1_out, PC___1, PCcheck;
  wire [24:0] addr;
  wire [31:0] _14, bit_extender_4_out, demultiplexer_1_out0, demultiplexer_1_out1, demultiplexer_4_out0,
       demultiplexer_4_out1, demultiplexer_4_out2, demultiplexer_4_out3, demultiplexer_4_out4,
       demultiplexer_4_out5, demultiplexer_4_out6, demultiplexer_4_out7, demultiplexer_4_out8,
       demultiplexer_4_out9, demultiplexer_4_out10, demultiplexer_4_out11, demultiplexer_4_out12,
       demultiplexer_4_out13, JAL, multiplexer_4_out, or_6_out, Out1, Out2, shifter_1_out, shifter_2_out,
       shifter_3_out, shifter_4_out, shifter_5_out, u_alu_1_alu_result, u_mem_1_data_out;

  Comparator #(.width(4), .mode("unsigned")) comparator_1 (
    .a(ctrl_op), .b(4'b1010), .lt(comparator_1_lt));  // open: gt, eq
  or or_1 (or_1_out, comparator_1_lt, not_1_out);
  not not_1 (not_1_out, bit_extender_1_out);
  and and_1 (and_1_out, comparator_3_eq, comparator_2_eq);
  Comparator #(.width(3), .mode("unsigned")) comparator_2 (.a(JC), .b(3'b111), .eq(comparator_2_eq));  // open: gt, lt
  assign RD = RD1 | RD2;  // OR_Gate or_2, 5 bits wide
  Bit_Extender #(.in_width(4), .out_width(1)) bit_extender_1 (.in(ctrl_op), .out(bit_extender_1_out));
  not not_2 (not_2_out, ZC);
  and and_2 (RD_WRITE_ENABLE, not_2_out, RD_WRITE_ENABLE_t);
  or or_3 (RD_WRITE_ENABLE_t, or_1_out, and_1_out);
  Comparator #(.width(4), .mode("unsigned")) comparator_3 (
    .a(ctrl_op), .b(4'b1111), .eq(comparator_3_eq));  // open: gt, lt
  Register #(.width(24)) PC (.D(multiplexer_1_out), .Q(FETCH_ADDRESS), .clk(CLOCK));  // open: en, clr
  Adder #(.width(24)) adder_1 (.a(FETCH_ADDRESS), .b(24'h1), .out(adder_1_out));  // open: cin, cout
  Multiplexer #(.width(24), .enable("false")) multiplexer_1 (
    .in0(adder_1_out), .in1(PCcheck), .out(multiplexer_1_out), .sel(and_3_out));
  and and_3 (and_3_out, comparator_4_eq, cond);
  Multiplexer #(.select(3), .width(24), .enable("false")) multiplexer_2 (
    .in0(jfinal), .in1(j_0out_t_t), .in2(j_0out_t), .in3(j_0out), .in4(j__0out_t), .in5(j__0out),
    .in6(j__0out_t_t), .in7(jfinal), .out(PCcheck), .sel(JC));
  Comparator #(.width(4), .mode("unsigned")) comparator_4 (
    .a(ctrl_op), .b(4'b1111), .eq(comparator_4_eq));  // open: gt, lt
  not not_3 (not_3_out, j_0_t_t);
  not not_4 (not_4_out, j_0_t);
  Demultiplexer #(.width(32), .enable("false")) demultiplexer_1 (
    .out0(demultiplexer_1_out0), .out1(demultiplexer_1_out1), .in(INSTRUCTION), .sel(comparator_5_eq));
  Shifter #(.width(32), .shift("lr")) shifter_1 (.in(INSTRUCTION), .\dist (5'b11011), .out(shifter_1_out));
  Bit_Extender #(.in_width(32), .out_width(5)) bit_extender_2 (.in(INSTRUCTION), .out(RI));
  Demultiplexer #(.width(24), .enable("false")) demultiplexer_2 (
    .out1(demultiplexer_2_out1), .in(adder_2_out), .sel(comparator_6_eq));  // open: out0
  Adder #(.width(24)) adder_2 (.a(FETCH_ADDRESS), .b(24'h1), .out(adder_2_out));  // open: cin, cout
  not not_5 (not_5_out, j_0);
  Shifter #(.width(32), .shift("lr")) shifter_2 (.in(INSTRUCTION), .\dist (5'b11100), .out(shifter_2_out));
  Comparator #(.width(4), .mode("unsigned")) comparator_5 (
    .a(ctrl_op), .b(4'b1111), .eq(comparator_5_eq));  // open: gt, lt
  Bit_Extender #(.in_width(32), .out_width(1)) bit_extender_3 (.in(shifter_1_out), .out(Imm));
  Demultiplexer #(.width(24), .enable("false")) demultiplexer_3 (
    .out1(demultiplexer_3_out1), .in(demultiplexer_2_out1), .sel(comparator_7_eq));  // open: out0
  Comparator #(.width(4), .mode("unsigned")) comparator_6 (
    .a(ctrl_op), .b(4'b1111), .eq(comparator_6_eq));  // open: gt, lt
  Multiplexer #(.select(3), .enable("false")) multiplexer_3 (
    .in0(1'b1), .in1(j_0_t_t), .in2(j_0_t), .in3(j_0), .in4(not_3_out), .in5(not_4_out), .in6(not_5_out),
    .in7(1'b1), .out(cond), .sel(JC));
  Multiplexer #(.width(32), .enable("false")) multiplexer_4 (
    .in0(RI_READ_VALUE), .in1(bit_extender_4_out), .out(multiplexer_4_out), .sel(Imm));
  assign bit_extender_4_out = {{15{ImmVal[16]}}, ImmVal};  // Bit_Extender bit_extender_4
  assign RD_WRITE_VALUE = Out1 | Out2 | _14 | JAL;  // OR_Gate or_4, 32 bits wide
  Bit_Extender #(.in_width(32), .out_width(4)) bit_extender_5 (.in(shifter_2_out), .out(ctrl_op));
  Bit_Extender #(.in_width(32), .out_width(17)) bit_extender_6 (.in(demultiplexer_1_out0), .out(ImmVal));
  Shifter #(.width(32), .shift("lr")) shifter_3 (.in(demultiplexer_1_out0), .\dist (5'b10110), .out(shifter_3_out));
  Shifter #(.width(32), .shift("lr")) shifter_4 (.in(demultiplexer_1_out0), .\dist (5'b10001), .out(shifter_4_out));
  Shifter #(.width(32), .shift("lr")) shifter_5 (.in(demultiplexer_1_out1), .\dist (5'b11000), .out(shifter_5_out));
  Bit_Extender #(.in_width(32)) bit_extender_7 (.in(demultiplexer_1_out1), .out(JVal));
  assign JAL = {{8{1'b0}}, demultiplexer_3_out1};  // Bit_Extender bit_extender_8
  Comparator #(.width(3), .mode("unsigned")) comparator_7 (.a(JC), .b(3'b111), .eq(comparator_7_eq));  // open: gt, lt
  Bit_Extender #(.in_width(32), .out_width(5)) bit_extender_9 (.in(shifter_3_out), .out(RD1));
  Bit_Extender #(.in_width(32), .out_width(5)) bit_extender_10 (.in(shifter_4_out), .out(RS));
  Bit_Extender #(.in_width(32), .out_width(3)) bit_extender_11 (.in(shifter_5_out), .out(JC));
  Comparator #(.width(5)) comparator_8 (.a(RD), .b({5{1'b0}}), .eq(ZC));  // open: gt, lt
  u_ALU u_alu_1 (
    .ALU_X(RS_READ_VALUE), .ALU_Y(multiplexer_4_out), .ALU_RESULT(u_alu_1_alu_result), .ALU_CONTROL(ctrl_op));
  Demultiplexer #(.select(4), .width(32), .enable("false")) demultiplexer_4 (
    .out0(demultiplexer_4_out0), .out1(demultiplexer_4_out1), .out2(demultiplexer_4_out2),
    .out3(demultiplexer_4_out3), .out4(demultiplexer_4_out4), .out5(demultiplexer_4_out5),
    .out6(demultiplexer_4_out6), .out7(demultiplexer_4_out7), .out8(demultiplexer_4_out8),
    .out9(demultiplexer_4_out9), .out10(demultiplexer_4_out10), .out11(demultiplexer_4_out11),
    .out12(demultiplexer_4_out12), .out13(demultiplexer_4_out13), .out14(_14), .in(u_alu_1_alu_result),
    .sel(ctrl_op));  // open: out15
  Shifter #(.width(4), .shift("lr")) shifter_6 (.in(ctrl_op), .\dist (2'b10), .out(shifter_6_out));
  Bit_Extender #(.in_width(4), .out_width(1)) bit_extender_12 (.in(shifter_6_out), .out(bit_extender_12_out));
  Demultiplexer #(.width(5), .enable("false")) demultiplexer_5 (
    .out1(demultiplexer_5_out1), .in(5'b00110), .sel(comparator_9_eq));  // open: out0
  Bit_Extender #(.in_width(4), .out_width(1)) bit_extender_13 (.in(ctrl_op), .out(bit_extender_13_out));
  Multiplexer #(.width(24), .enable("false")) multiplexer_5 (.in0(PC___1), .in1(jfinal), .out(j_0out_t), .sel(j_0_t));
  Demultiplexer #(.width(5), .enable("false")) demultiplexer_6 (
    .out1(RD2), .in(demultiplexer_5_out1), .sel(comparator_11_eq));  // open: out0
  Comparator #(.width(4), .mode("unsigned")) comparator_9 (
    .a(ctrl_op), .b(4'b1111), .eq(comparator_9_eq));  // open: gt, lt
  Adder #(.width(24)) adder_3 (.a(FETCH_ADDRESS), .b(24'h1), .out(PC___1));  // open: cin, cout
  assign Out1 = demultiplexer_4_out0 | demultiplexer_4_out1 | demultiplexer_4_out2 | demultiplexer_4_out3 | demultiplexer_4_out4 | demultiplexer_4_out5 | demultiplexer_4_out6 | demultiplexer_4_out7 | demultiplexer_4_out8 | demultiplexer_4_out9;  // OR_Gate or_5, 32 bits wide
  u_MEM u_mem_1 (
    .ADDRESS(addr), .WORD_MODE(bit_extender_12_out), .MEM_WRITE(bit_extender_13_out),
    .DATA_IN(RD_READ_VALUE), .CLOCK(CLOCK), .DATA_OUT(u_mem_1_data_out));  // open: Even_Addr, Even_Data, Odd_Addr, Odd_Data
  Comparator #(.width(32)) comparator_10 (.a(JC_READ_VALUE), .b({32{1'b0}}), .gt(j_0_t_t), .eq(j_0_t), .lt(j_0));
  Comparator #(.width(3), .mode("unsigned")) comparator_11 (.a(JC), .b(3'b111), .eq(comparator_11_eq));  // open: gt, lt
  assign or_6_out = demultiplexer_4_out10 | demultiplexer_4_out11 | demultiplexer_4_out12 | demultiplexer_4_out13;  // OR_Gate or_6, 32 bits wide
  Bit_Extender #(.in_width(32), .out_width(25)) bit_extender_14 (.in(or_6_out), .out(addr));
  Multiplexer #(.width(32), .enable("false")) multiplexer_6 (
    .in0({32{1'b0}}), .in1(u_mem_1_data_out), .out(Out2), .sel(and_4_out));
  and and_4 (and_4_out, comparator_12_gt, RD_WRITE_ENABLE_t, comparator_14_lt);
  Comparator #(.width(4), .mode("unsigned")) comparator_12 (
    .a(ctrl_op), .b(4'b1001), .gt(comparator_12_gt));  // open: eq, lt
  Comparator #(.width(4)) comparator_13 (.a(ctrl_op), .b(4'b1111), .eq(jump));  // open: gt, lt
  Bit_Extender #(.in_width(32), .out_width(24)) bit_extender_15 (.in(RI_READ_VALUE), .out(bit_extender_15_out));
  assign bit_extender_16_out = {{8{1'b0}}, JVal};  // Bit_Extender bit_extender_16
  Multiplexer #(.width(24), .enable("false")) multiplexer_7 (.in0(PC___1), .in1(jfinal), .out(j_0out), .sel(j_0));
  not not_6 (not_6_out, j_0);
  not not_7 (not_7_out, j_0_t);
  Comparator #(.width(4), .mode("unsigned")) comparator_14 (
    .a(ctrl_op), .b(4'b1110), .lt(comparator_14_lt));  // open: gt, eq
  Multiplexer #(.width(24), .enable("false")) multiplexer_8 (
    .in0(bit_extender_15_out), .in1(bit_extender_16_out), .out(jfinal), .sel(Imm));
  Multiplexer #(.width(24), .enable("false")) multiplexer_9 (
    .in0(PC___1), .in1(jfinal), .out(j__0out_t_t), .sel(not_6_out));
  Multiplexer #(.width(24), .enable("false")) multiplexer_10 (
    .in0(PC___1), .in1(jfinal), .out(j__0out), .sel(not_7_out));
  Multiplexer #(.width(24), .enable("false")) multiplexer_11 (
    .in0(PC___1), .in1(jfinal), .out(j_0out_t_t), .sel(j_0_t_t));
  not not_8 (not_8_out, j_0_t_t);
  Multiplexer #(.width(24), .enable("false")) multiplexer_12 (
    .in0(PC___1), .in1(jfinal), .out(j__out), .sel(not_8_out));

  // Other names for the same wires on the sheet: clk = CLOCK; JCR[31:0] = JC_READ_VALUE; FA[23:0] = FETCH_ADDRESS;
  //   PC[23:0] = FETCH_ADDRESS; result[31:0] = RD_WRITE_VALUE

  // Notes on the sheet:
  //   Feel free to use these ALU/MEM components, or delete them!
endmodule

module u_ALU (
  input  [31:0] ALU_X,
  input  [31:0] ALU_Y,
  input  [3:0] ALU_CONTROL,
  output [31:0] ALU_RESULT
);

  wire comparator_1_eq, comparator_2_eq, sign;
  wire [4:0] bit_extender_1_out, bit_extender_2_out;
  wire [14:0] bit_extender_3_out;
  wire [16:0] bit_extender_4_out;
  wire [31:0] bit_extender_5_out, bit_extender_6_out, divider_1_out, divr, multiplexer_1_out,
       multiplexer_4_out, multiplexer_5_out, negator_1_out, negator_2_out, result0, result1, result2,
       result3, result4, result5, result6, result7, result8, result9, result14, shifter_2_out, shifter_3_out;

  u_ShiftL u_shiftl_1 (.in_1(ALU_X), .result1(result0), .in_2(ALU_Y));
  Bit_Extender #(.in_width(32), .out_width(5)) bit_extender_1 (.in(ALU_Y), .out(bit_extender_1_out));
  Bit_Extender #(.in_width(32), .out_width(5)) bit_extender_2 (.in(ALU_Y), .out(bit_extender_2_out));
  Shifter #(.width(32), .shift("ar")) shifter_1 (.in(ALU_X), .\dist (bit_extender_1_out), .out(result1));
  assign result2 = ALU_X & ALU_Y;  // AND_Gate and_1, 32 bits wide
  assign result3 = ALU_X | ALU_Y;  // OR_Gate or_1, 32 bits wide
  u_REV u_rev_1 (.INPUT(ALU_X), .REVERSE_AMOUNT(bit_extender_2_out), .OUTPUT(result4));
  assign result5 = ALU_X ^ ALU_Y;  // XOR_Gate xor_1, 32 bits wide
  Adder #(.width(32)) adder_1 (.a(ALU_X), .b(ALU_Y), .out(result6));  // open: cin, cout
  Subtractor #(.width(32)) subtractor_1 (.a(ALU_X), .b(ALU_Y), .out(result7));  // open: bin, bout
  Multiplier #(.width(32)) multiplier_1 (.a(ALU_X), .b(ALU_Y), .out(result8));  // open: cin, cout
  Bit_Extender #(.in_width(32), .out_width(15)) bit_extender_3 (.in(ALU_X), .out(bit_extender_3_out));
  Bit_Extender #(.in_width(32), .out_width(17)) bit_extender_4 (.in(ALU_Y), .out(bit_extender_4_out));
  assign bit_extender_5_out = {{17{1'b0}}, bit_extender_3_out};  // Bit_Extender bit_extender_5
  assign bit_extender_6_out = {{15{1'b0}}, bit_extender_4_out};  // Bit_Extender bit_extender_6
  Shifter #(.width(32)) shifter_2 (.in(bit_extender_6_out), .\dist (5'b01111), .out(shifter_2_out));
  Multiplexer #(.width(32), .enable("false")) multiplexer_1 (
    .in0(32'h7fffffff), .in1({32{1'b0}}), .out(multiplexer_1_out), .sel(comparator_2_eq));
  assign result14 = bit_extender_5_out | shifter_2_out;  // OR_Gate or_2, 32 bits wide
  Comparator #(.width(32)) comparator_1 (.a(ALU_Y), .b({32{1'b0}}), .eq(comparator_1_eq));  // open: gt, lt
  Multiplexer #(.select(4), .width(32), .enable("false")) multiplexer_2 (
    .in0(result0), .in1(result1), .in2(result2), .in3(result3), .in4(result4), .in5(result5), .in6(result6),
    .in7(result7), .in8(result8), .in9(result9), .in10(result6), .in11(result6), .in12(result6),
    .in13(result6), .in14(result14), .in15({32{1'b0}}), .out(ALU_RESULT), .sel(ALU_CONTROL));
  Multiplexer #(.width(32), .enable("false")) multiplexer_3 (
    .in0(divr), .in1(multiplexer_4_out), .out(result9), .sel(comparator_1_eq));
  Multiplexer #(.width(32), .enable("false")) multiplexer_4 (
    .in0(multiplexer_1_out), .in1(32'h80000000), .out(multiplexer_4_out), .sel(sign));
  Shifter #(.width(32), .shift("lr")) shifter_3 (.in(ALU_X), .\dist ({5{1'b1}}), .out(shifter_3_out));
  Comparator #(.width(32)) comparator_2 (.a(ALU_X), .b({32{1'b0}}), .eq(comparator_2_eq));  // open: gt, lt
  Bit_Extender #(.in_width(32), .out_width(1)) bit_extender_7 (.in(shifter_3_out), .out(sign));
  Negator #(.width(32)) negator_1 (.in(ALU_X), .out(negator_1_out));
  Multiplexer #(.width(32), .enable("false")) multiplexer_5 (
    .in0(ALU_X), .in1(negator_1_out), .out(multiplexer_5_out), .sel(sign));
  Divider #(.width(32)) divider_1 (.a(multiplexer_5_out), .b(ALU_Y), .out(divider_1_out));  // open: upper, rem
  Multiplexer #(.width(32), .enable("false")) multiplexer_6 (
    .in0(divider_1_out), .in1(negator_2_out), .out(divr), .sel(sign));
  Negator #(.width(32)) negator_2 (.in(divider_1_out), .out(negator_2_out));

  // Other names for the same wires on the sheet: result[31:0] = ALU_RESULT; Source1[31:0] = ALU_X;
  //   Source2[31:0] = ALU_Y

  // Notes on the sheet:
  //   Feel free to use this component, or not, however you want!
endmodule

// Data Memory
module u_MEM (
  input  [24:0] ADDRESS,
  input  WORD_MODE,
  input  MEM_WRITE,
  input  [31:0] DATA_IN,
  input  CLOCK,
  output [31:0] DATA_OUT,
  output [23:0] Even_Addr,
  output [23:0] Odd_Addr,
  output [15:0] Odd_Data,
  output [15:0] Even_Data
);

  wire and_2_out, and_3_out, and_4_out, and_6_out, and_7_out, and_8_out, ld2, LSBit, not_1_out, not_2_out,
       not_3_out, not_4_out, not_5_out, not_6_out, not_7_out, not_8_out, or_1_out, or_4_out, or_5_out,
       or_8_out, str2;
  wire [15:0] bit_extender_3_out, demultiplexer_3_out0, demultiplexer_4_out0, demultiplexer_4_out1, HW_Odd,
       multiplexer_2_out, result1, result2, S1, S2;
  wire [23:0] bit_extender_2_out, demultiplexer_2_out0, EvenOut1, EvenOut2, multiplexer_1_out, OddOut1,
       OddOut2;
  wire [24:0] shifter_1_out;
  wire [31:0] bit_extender_4_out, bit_extender_5_out, bit_extender_6_out, bit_extender_7_out,
       bit_extender_8_out, demultiplexer_5_out0, demultiplexer_5_out1, multiplexer_3_out, multiplexer_4_out,
       multiplexer_6_out, r0, r1, shifter_2_out, shifter_3_out;

  and and_1 (str2, MEM_WRITE, or_1_out);
  and and_2 (and_2_out, not_1_out, not_2_out);
  not not_1 (not_1_out, WORD_MODE);
  or or_1 (or_1_out, and_2_out, WORD_MODE);
  not not_2 (not_2_out, LSBit);
  assign Odd_Addr = OddOut1 | OddOut2;  // OR_Gate or_2, 24 bits wide
  assign Odd_Data = S2 | HW_Odd | S1;  // OR_Gate or_3, 16 bits wide
  not not_3 (not_3_out, WORD_MODE);
  and and_3 (and_3_out, MEM_WRITE, or_4_out);
  or or_4 (or_4_out, and_4_out, WORD_MODE);
  and and_4 (and_4_out, not_3_out, LSBit);
  Multiplexer #(.width(24), .enable("false")) multiplexer_1 (
    .in0({24{1'b0}}), .in1(24'h1), .out(multiplexer_1_out), .sel(LSBit));
  RAM #(.addrWidth(24), .dataWidth(16), .bus("separate")) ram_1 (
    .addr(Odd_Addr), .din(Odd_Data), .data(result1), .str(and_3_out), .clk(CLOCK), .ld(and_7_out));  // open: sel, clr
  and and_5 (ld2, not_4_out, or_5_out);
  or or_5 (or_5_out, and_6_out, WORD_MODE);
  not not_4 (not_4_out, MEM_WRITE);
  and and_6 (and_6_out, not_5_out, not_6_out);
  not not_5 (not_5_out, WORD_MODE);
  not not_6 (not_6_out, LSBit);
  Bit_Extender #(.in_width(25), .out_width(1)) bit_extender_1 (.in(ADDRESS), .out(LSBit));
  assign Even_Addr = EvenOut1 | EvenOut2;  // OR_Gate or_6, 24 bits wide
  and and_7 (and_7_out, not_7_out, or_8_out);
  not not_7 (not_7_out, MEM_WRITE);
  and and_8 (and_8_out, not_8_out, LSBit);
  not not_8 (not_8_out, WORD_MODE);
  Adder #(.width(24)) adder_1 (.a(multiplexer_1_out), .b(OddOut2), .out(EvenOut2));  // open: cin, cout
  assign Even_Data = demultiplexer_4_out1 | demultiplexer_4_out0 | demultiplexer_3_out0;  // OR_Gate or_7, 16 bits wide
  or or_8 (or_8_out, and_8_out, WORD_MODE);
  Demultiplexer #(.width(24), .enable("false")) demultiplexer_1 (
    .out0(EvenOut1), .out1(OddOut1), .in(demultiplexer_2_out0), .sel(LSBit));
  Demultiplexer #(.width(24), .enable("false")) demultiplexer_2 (
    .out0(demultiplexer_2_out0), .out1(OddOut2), .in(bit_extender_2_out), .sel(WORD_MODE));
  RAM #(.addrWidth(24), .dataWidth(16), .bus("separate")) ram_2 (
    .addr(Even_Addr), .din(Even_Data), .data(result2), .str(str2), .clk(CLOCK), .ld(ld2));  // open: sel, clr
  Shifter #(.width(25), .shift("lr")) shifter_1 (.in(ADDRESS), .\dist (5'b00001), .out(shifter_1_out));
  Demultiplexer #(.width(16), .enable("false")) demultiplexer_3 (
    .out0(demultiplexer_3_out0), .out1(HW_Odd), .in(bit_extender_3_out), .sel(LSBit));
  Demultiplexer #(.width(32), .enable("false")) demultiplexer_4 (
    .out0({demultiplexer_4_out0, S1}), .out1({S2, demultiplexer_4_out1}), .in(demultiplexer_5_out1),
    .sel(LSBit));
  Bit_Extender #(.in_width(25), .out_width(24)) bit_extender_2 (.in(shifter_1_out), .out(bit_extender_2_out));
  Bit_Extender #(.in_width(32)) bit_extender_3 (.in(demultiplexer_5_out0), .out(bit_extender_3_out));
  Demultiplexer #(.width(32), .enable("false")) demultiplexer_5 (
    .out0(demultiplexer_5_out0), .out1(demultiplexer_5_out1), .in(DATA_IN), .sel(WORD_MODE));
  Multiplexer #(.width(16), .enable("false")) multiplexer_2 (
    .in0(result2), .in1(result1), .out(multiplexer_2_out), .sel(LSBit));
  assign bit_extender_4_out = {{16{1'b0}}, result1};  // Bit_Extender bit_extender_4
  Shifter #(.width(32)) shifter_2 (.in(bit_extender_4_out), .\dist (5'b10000), .out(shifter_2_out));
  assign bit_extender_5_out = {{16{1'b0}}, result2};  // Bit_Extender bit_extender_5
  assign bit_extender_6_out = {{16{1'b0}}, result2};  // Bit_Extender bit_extender_6
  Shifter #(.width(32)) shifter_3 (.in(bit_extender_6_out), .\dist (5'b10000), .out(shifter_3_out));
  assign bit_extender_7_out = {{16{1'b0}}, result1};  // Bit_Extender bit_extender_7
  assign bit_extender_8_out = {{16{multiplexer_2_out[15]}}, multiplexer_2_out};  // Bit_Extender bit_extender_8
  assign r1 = shifter_2_out | bit_extender_5_out;  // OR_Gate or_9, 32 bits wide
  assign r0 = shifter_3_out | bit_extender_7_out;  // OR_Gate or_10, 32 bits wide
  Multiplexer #(.width(32), .enable("false")) multiplexer_3 (
    .in0(bit_extender_8_out), .in1({32{1'b0}}), .out(multiplexer_3_out), .sel(MEM_WRITE));
  Multiplexer #(.width(32), .enable("false")) multiplexer_4 (.in0(r0), .in1(r1), .out(multiplexer_4_out), .sel(LSBit));
  Multiplexer #(.width(32), .enable("false")) multiplexer_5 (
    .in0(multiplexer_3_out), .in1(multiplexer_6_out), .out(DATA_OUT), .sel(WORD_MODE));
  Multiplexer #(.width(32), .enable("false")) multiplexer_6 (
    .in0(multiplexer_4_out), .in1({32{1'b0}}), .out(multiplexer_6_out), .sel(MEM_WRITE));

  // Other names for the same wires on the sheet: Add[24:0] = ADDRESS; CLK = CLOCK; Data[31:0] = DATA_IN;
  //   result[31:0] = DATA_OUT; Str = MEM_WRITE; WM = WORD_MODE

  // Notes on the sheet:
  //   Feel free to use this component, or not, however you want!
  //   You might use the word mode input to differentiate LW/SW from LH/SH.
  //   However, you *SHOULD* use 2 RAM modules, one for even addresses and one for odd addresses.
endmodule

module u_REV (
  input  [4:0] REVERSE_AMOUNT,
  input  [31:0] INPUT,
  output [31:0] OUTPUT
);

  wire u_in2out1_1_lower_output, u_in2out1_1_upper_output, u_in2out1_2_lower_output,
       u_in2out1_2_upper_output, u_in2out1_3_lower_output, u_in2out1_3_upper_output,
       u_in2out1_4_lower_output, u_in2out1_4_upper_output, u_in2out1_5_lower_output,
       u_in2out1_5_upper_output, u_in2out1_6_lower_output, u_in2out1_6_upper_output,
       u_in2out1_7_lower_output, u_in2out1_7_upper_output, u_in2out1_8_lower_output,
       u_in2out1_8_upper_output, u_in2out1_9_lower_output, u_in2out1_9_upper_output,
       u_in2out1_10_lower_output, u_in2out1_10_upper_output, u_in2out1_11_lower_output,
       u_in2out1_11_upper_output, u_in2out1_12_lower_output, u_in2out1_12_upper_output,
       u_in2out1_13_lower_output, u_in2out1_13_upper_output, u_in2out1_14_lower_output,
       u_in2out1_14_upper_output, u_in2out1_15_lower_output, u_in2out1_15_upper_output,
       u_in2out1_16_lower_output, u_in2out1_16_upper_output;
  wire [1:0] u_in4out2_1_lower_output, u_in4out2_1_upper_output, u_in4out2_2_lower_output,
       u_in4out2_2_upper_output, u_in4out2_3_lower_output, u_in4out2_3_upper_output,
       u_in4out2_4_lower_output, u_in4out2_4_upper_output, u_in4out2_5_lower_output,
       u_in4out2_5_upper_output, u_in4out2_6_lower_output, u_in4out2_6_upper_output,
       u_in4out2_7_lower_output, u_in4out2_7_upper_output, u_in4out2_8_lower_output, u_in4out2_8_upper_output;
  wire [3:0] u_in8out4_1_lower_output, u_in8out4_1_upper_output, u_in8out4_2_lower_output,
       u_in8out4_2_upper_output, u_in8out4_3_lower_output, u_in8out4_3_upper_output,
       u_in8out4_4_lower_output, u_in8out4_4_upper_output;
  wire [7:0] u_in16out8_1_lower_output, u_in16out8_1_upper_output, u_in16out8_2_lower_output,
       u_in16out8_2_upper_output;
  wire [15:0] u_in32out16_1_lower_output, u_in32out16_1_upper_output;
  wire [31:0] bit_extender_1_out, bit_extender_2_out, bit_extender_3_out, bit_extender_4_out,
       bit_extender_5_out, bit_extender_6_out, bit_extender_7_out, bit_extender_8_out, bit_extender_9_out,
       bit_extender_10_out, bit_extender_11_out, bit_extender_12_out, bit_extender_13_out,
       bit_extender_14_out, bit_extender_15_out, bit_extender_16_out, bit_extender_17_out,
       bit_extender_18_out, bit_extender_19_out, bit_extender_20_out, bit_extender_21_out,
       bit_extender_22_out, bit_extender_23_out, bit_extender_24_out, bit_extender_25_out,
       bit_extender_26_out, bit_extender_27_out, bit_extender_28_out, bit_extender_29_out,
       bit_extender_30_out, bit_extender_31_out, bit_extender_32_out, shifter_1_out, shifter_2_out,
       shifter_3_out, shifter_4_out, shifter_5_out, shifter_6_out, shifter_7_out, shifter_8_out,
       shifter_9_out, shifter_10_out, shifter_11_out, shifter_12_out, shifter_13_out, shifter_14_out,
       shifter_15_out, shifter_16_out, shifter_17_out, shifter_18_out, shifter_19_out, shifter_20_out,
       shifter_21_out, shifter_22_out, shifter_23_out, shifter_24_out, shifter_25_out, shifter_26_out,
       shifter_27_out, shifter_28_out, shifter_29_out, shifter_30_out, shifter_31_out, shifter_32_out;

  u_in32out16 u_in32out16_1 (
    .data_in(INPUT), .\input (REVERSE_AMOUNT[4]), .upper_output(u_in32out16_1_upper_output),
    .lower_output(u_in32out16_1_lower_output));
  u_in16out8 u_in16out8_1 (
    .data_in(u_in32out16_1_upper_output), .\input (REVERSE_AMOUNT[3]),
    .upper_output(u_in16out8_1_upper_output), .lower_output(u_in16out8_1_lower_output));
  u_in16out8 u_in16out8_2 (
    .data_in(u_in32out16_1_lower_output), .\input (REVERSE_AMOUNT[3]),
    .upper_output(u_in16out8_2_upper_output), .lower_output(u_in16out8_2_lower_output));
  u_in8out4 u_in8out4_1 (
    .data_in(u_in16out8_1_upper_output), .\input (REVERSE_AMOUNT[2]),
    .upper_output(u_in8out4_1_upper_output), .lower_output(u_in8out4_1_lower_output));
  u_in8out4 u_in8out4_2 (
    .data_in(u_in16out8_1_lower_output), .\input (REVERSE_AMOUNT[2]),
    .upper_output(u_in8out4_2_upper_output), .lower_output(u_in8out4_2_lower_output));
  u_in8out4 u_in8out4_3 (
    .data_in(u_in16out8_2_upper_output), .\input (REVERSE_AMOUNT[2]),
    .upper_output(u_in8out4_3_upper_output), .lower_output(u_in8out4_3_lower_output));
  u_in8out4 u_in8out4_4 (
    .data_in(u_in16out8_2_lower_output), .\input (REVERSE_AMOUNT[2]),
    .upper_output(u_in8out4_4_upper_output), .lower_output(u_in8out4_4_lower_output));
  u_in4out2 u_in4out2_1 (
    .data_in(u_in8out4_1_upper_output), .\input (REVERSE_AMOUNT[1]), .upper_output(u_in4out2_1_upper_output),
    .lower_output(u_in4out2_1_lower_output));
  u_in4out2 u_in4out2_2 (
    .data_in(u_in8out4_1_lower_output), .\input (REVERSE_AMOUNT[1]), .upper_output(u_in4out2_2_upper_output),
    .lower_output(u_in4out2_2_lower_output));
  u_in4out2 u_in4out2_3 (
    .data_in(u_in8out4_2_upper_output), .\input (REVERSE_AMOUNT[1]), .upper_output(u_in4out2_3_upper_output),
    .lower_output(u_in4out2_3_lower_output));
  u_in4out2 u_in4out2_4 (
    .data_in(u_in8out4_2_lower_output), .\input (REVERSE_AMOUNT[1]), .upper_output(u_in4out2_4_upper_output),
    .lower_output(u_in4out2_4_lower_output));
  u_in4out2 u_in4out2_5 (
    .data_in(u_in8out4_3_upper_output), .\input (REVERSE_AMOUNT[1]), .upper_output(u_in4out2_5_upper_output),
    .lower_output(u_in4out2_5_lower_output));
  u_in4out2 u_in4out2_6 (
    .data_in(u_in8out4_3_lower_output), .\input (REVERSE_AMOUNT[1]), .upper_output(u_in4out2_6_upper_output),
    .lower_output(u_in4out2_6_lower_output));
  u_in4out2 u_in4out2_7 (
    .data_in(u_in8out4_4_upper_output), .\input (REVERSE_AMOUNT[1]), .upper_output(u_in4out2_7_upper_output),
    .lower_output(u_in4out2_7_lower_output));
  u_in4out2 u_in4out2_8 (
    .data_in(u_in8out4_4_lower_output), .\input (REVERSE_AMOUNT[1]), .upper_output(u_in4out2_8_upper_output),
    .lower_output(u_in4out2_8_lower_output));
  u_in2out1 u_in2out1_1 (
    .data_in(u_in4out2_1_upper_output), .\input (REVERSE_AMOUNT[0]), .upper_output(u_in2out1_1_upper_output),
    .lower_output(u_in2out1_1_lower_output));
  u_in2out1 u_in2out1_2 (
    .data_in(u_in4out2_1_lower_output), .\input (REVERSE_AMOUNT[0]), .upper_output(u_in2out1_2_upper_output),
    .lower_output(u_in2out1_2_lower_output));
  u_in2out1 u_in2out1_3 (
    .data_in(u_in4out2_2_upper_output), .\input (REVERSE_AMOUNT[0]), .upper_output(u_in2out1_3_upper_output),
    .lower_output(u_in2out1_3_lower_output));
  u_in2out1 u_in2out1_4 (
    .data_in(u_in4out2_2_lower_output), .\input (REVERSE_AMOUNT[0]), .upper_output(u_in2out1_4_upper_output),
    .lower_output(u_in2out1_4_lower_output));
  u_in2out1 u_in2out1_5 (
    .data_in(u_in4out2_3_upper_output), .\input (REVERSE_AMOUNT[0]), .upper_output(u_in2out1_5_upper_output),
    .lower_output(u_in2out1_5_lower_output));
  u_in2out1 u_in2out1_6 (
    .data_in(u_in4out2_3_lower_output), .\input (REVERSE_AMOUNT[0]), .upper_output(u_in2out1_6_upper_output),
    .lower_output(u_in2out1_6_lower_output));
  u_in2out1 u_in2out1_7 (
    .data_in(u_in4out2_4_upper_output), .\input (REVERSE_AMOUNT[0]), .upper_output(u_in2out1_7_upper_output),
    .lower_output(u_in2out1_7_lower_output));
  u_in2out1 u_in2out1_8 (
    .data_in(u_in4out2_4_lower_output), .\input (REVERSE_AMOUNT[0]), .upper_output(u_in2out1_8_upper_output),
    .lower_output(u_in2out1_8_lower_output));
  u_in2out1 u_in2out1_9 (
    .data_in(u_in4out2_5_upper_output), .\input (REVERSE_AMOUNT[0]), .upper_output(u_in2out1_9_upper_output),
    .lower_output(u_in2out1_9_lower_output));
  u_in2out1 u_in2out1_10 (
    .data_in(u_in4out2_5_lower_output), .\input (REVERSE_AMOUNT[0]),
    .upper_output(u_in2out1_10_upper_output), .lower_output(u_in2out1_10_lower_output));
  u_in2out1 u_in2out1_11 (
    .data_in(u_in4out2_6_upper_output), .\input (REVERSE_AMOUNT[0]),
    .upper_output(u_in2out1_11_upper_output), .lower_output(u_in2out1_11_lower_output));
  u_in2out1 u_in2out1_12 (
    .data_in(u_in4out2_6_lower_output), .\input (REVERSE_AMOUNT[0]),
    .upper_output(u_in2out1_12_upper_output), .lower_output(u_in2out1_12_lower_output));
  u_in2out1 u_in2out1_13 (
    .data_in(u_in4out2_7_upper_output), .\input (REVERSE_AMOUNT[0]),
    .upper_output(u_in2out1_13_upper_output), .lower_output(u_in2out1_13_lower_output));
  u_in2out1 u_in2out1_14 (
    .data_in(u_in4out2_7_lower_output), .\input (REVERSE_AMOUNT[0]),
    .upper_output(u_in2out1_14_upper_output), .lower_output(u_in2out1_14_lower_output));
  u_in2out1 u_in2out1_15 (
    .data_in(u_in4out2_8_upper_output), .\input (REVERSE_AMOUNT[0]),
    .upper_output(u_in2out1_15_upper_output), .lower_output(u_in2out1_15_lower_output));
  u_in2out1 u_in2out1_16 (
    .data_in(u_in4out2_8_lower_output), .\input (REVERSE_AMOUNT[0]),
    .upper_output(u_in2out1_16_upper_output), .lower_output(u_in2out1_16_lower_output));
  assign bit_extender_1_out = {{31{1'b0}}, u_in2out1_1_upper_output};  // Bit_Extender bit_extender_1
  assign bit_extender_2_out = {{31{1'b0}}, u_in2out1_2_upper_output};  // Bit_Extender bit_extender_2
  assign bit_extender_3_out = {{31{1'b0}}, u_in2out1_3_upper_output};  // Bit_Extender bit_extender_3
  assign bit_extender_4_out = {{31{1'b0}}, u_in2out1_4_upper_output};  // Bit_Extender bit_extender_4
  assign bit_extender_5_out = {{31{1'b0}}, u_in2out1_5_upper_output};  // Bit_Extender bit_extender_5
  assign bit_extender_6_out = {{31{1'b0}}, u_in2out1_6_upper_output};  // Bit_Extender bit_extender_6
  assign bit_extender_7_out = {{31{1'b0}}, u_in2out1_7_upper_output};  // Bit_Extender bit_extender_7
  assign bit_extender_8_out = {{31{1'b0}}, u_in2out1_8_upper_output};  // Bit_Extender bit_extender_8
  assign bit_extender_9_out = {{31{1'b0}}, u_in2out1_9_upper_output};  // Bit_Extender bit_extender_9
  assign bit_extender_10_out = {{31{1'b0}}, u_in2out1_10_upper_output};  // Bit_Extender bit_extender_10
  assign bit_extender_11_out = {{31{1'b0}}, u_in2out1_11_upper_output};  // Bit_Extender bit_extender_11
  assign bit_extender_12_out = {{31{1'b0}}, u_in2out1_12_upper_output};  // Bit_Extender bit_extender_12
  assign bit_extender_13_out = {{31{1'b0}}, u_in2out1_13_upper_output};  // Bit_Extender bit_extender_13
  assign bit_extender_14_out = {{31{1'b0}}, u_in2out1_14_upper_output};  // Bit_Extender bit_extender_14
  assign bit_extender_15_out = {{31{1'b0}}, u_in2out1_15_upper_output};  // Bit_Extender bit_extender_15
  assign bit_extender_16_out = {{31{1'b0}}, u_in2out1_16_upper_output};  // Bit_Extender bit_extender_16
  assign bit_extender_17_out = {{31{1'b0}}, u_in2out1_1_lower_output};  // Bit_Extender bit_extender_17
  assign bit_extender_18_out = {{31{1'b0}}, u_in2out1_2_lower_output};  // Bit_Extender bit_extender_18
  assign bit_extender_19_out = {{31{1'b0}}, u_in2out1_3_lower_output};  // Bit_Extender bit_extender_19
  assign bit_extender_20_out = {{31{1'b0}}, u_in2out1_4_lower_output};  // Bit_Extender bit_extender_20
  assign bit_extender_21_out = {{31{1'b0}}, u_in2out1_5_lower_output};  // Bit_Extender bit_extender_21
  assign bit_extender_22_out = {{31{1'b0}}, u_in2out1_6_lower_output};  // Bit_Extender bit_extender_22
  assign bit_extender_23_out = {{31{1'b0}}, u_in2out1_7_lower_output};  // Bit_Extender bit_extender_23
  assign bit_extender_24_out = {{31{1'b0}}, u_in2out1_8_lower_output};  // Bit_Extender bit_extender_24
  assign bit_extender_25_out = {{31{1'b0}}, u_in2out1_9_lower_output};  // Bit_Extender bit_extender_25
  assign bit_extender_26_out = {{31{1'b0}}, u_in2out1_10_lower_output};  // Bit_Extender bit_extender_26
  assign bit_extender_27_out = {{31{1'b0}}, u_in2out1_11_lower_output};  // Bit_Extender bit_extender_27
  assign bit_extender_28_out = {{31{1'b0}}, u_in2out1_12_lower_output};  // Bit_Extender bit_extender_28
  assign bit_extender_29_out = {{31{1'b0}}, u_in2out1_13_lower_output};  // Bit_Extender bit_extender_29
  assign bit_extender_30_out = {{31{1'b0}}, u_in2out1_14_lower_output};  // Bit_Extender bit_extender_30
  assign bit_extender_31_out = {{31{1'b0}}, u_in2out1_15_lower_output};  // Bit_Extender bit_extender_31
  assign bit_extender_32_out = {{31{1'b0}}, u_in2out1_16_lower_output};  // Bit_Extender bit_extender_32
  Shifter #(.width(32)) shifter_1 (.in(bit_extender_1_out), .\dist ({5{1'b1}}), .out(shifter_1_out));
  Shifter #(.width(32)) shifter_2 (.in(bit_extender_17_out), .\dist (5'b11110), .out(shifter_2_out));
  Shifter #(.width(32)) shifter_3 (.in(bit_extender_2_out), .\dist (5'b11101), .out(shifter_3_out));
  Shifter #(.width(32)) shifter_4 (.in(bit_extender_18_out), .\dist (5'b11100), .out(shifter_4_out));
  Shifter #(.width(32)) shifter_5 (.in(bit_extender_3_out), .\dist (5'b11011), .out(shifter_5_out));
  Shifter #(.width(32)) shifter_6 (.in(bit_extender_19_out), .\dist (5'b11010), .out(shifter_6_out));
  Shifter #(.width(32)) shifter_7 (.in(bit_extender_4_out), .\dist (5'b11001), .out(shifter_7_out));
  Shifter #(.width(32)) shifter_8 (.in(bit_extender_20_out), .\dist (5'b11000), .out(shifter_8_out));
  Shifter #(.width(32)) shifter_9 (.in(bit_extender_5_out), .\dist (5'b10111), .out(shifter_9_out));
  Shifter #(.width(32)) shifter_10 (.in(bit_extender_21_out), .\dist (5'b10110), .out(shifter_10_out));
  Shifter #(.width(32)) shifter_11 (.in(bit_extender_6_out), .\dist (5'b10101), .out(shifter_11_out));
  Shifter #(.width(32)) shifter_12 (.in(bit_extender_22_out), .\dist (5'b10100), .out(shifter_12_out));
  Shifter #(.width(32)) shifter_13 (.in(bit_extender_7_out), .\dist (5'b10011), .out(shifter_13_out));
  Shifter #(.width(32)) shifter_14 (.in(bit_extender_23_out), .\dist (5'b10010), .out(shifter_14_out));
  Shifter #(.width(32)) shifter_15 (.in(bit_extender_8_out), .\dist (5'b10001), .out(shifter_15_out));
  Shifter #(.width(32)) shifter_16 (.in(bit_extender_24_out), .\dist (5'b10000), .out(shifter_16_out));
  Shifter #(.width(32)) shifter_17 (.in(bit_extender_9_out), .\dist (5'b01111), .out(shifter_17_out));
  Shifter #(.width(32)) shifter_18 (.in(bit_extender_25_out), .\dist (5'b01110), .out(shifter_18_out));
  Shifter #(.width(32)) shifter_19 (.in(bit_extender_10_out), .\dist (5'b01101), .out(shifter_19_out));
  Shifter #(.width(32)) shifter_20 (.in(bit_extender_26_out), .\dist (5'b01100), .out(shifter_20_out));
  Shifter #(.width(32)) shifter_21 (.in(bit_extender_11_out), .\dist (5'b01011), .out(shifter_21_out));
  Shifter #(.width(32)) shifter_22 (.in(bit_extender_27_out), .\dist (5'b01010), .out(shifter_22_out));
  Shifter #(.width(32)) shifter_23 (.in(bit_extender_12_out), .\dist (5'b01001), .out(shifter_23_out));
  Shifter #(.width(32)) shifter_24 (.in(bit_extender_28_out), .\dist (5'b01000), .out(shifter_24_out));
  Shifter #(.width(32)) shifter_25 (.in(bit_extender_13_out), .\dist (5'b00111), .out(shifter_25_out));
  Shifter #(.width(32)) shifter_26 (.in(bit_extender_29_out), .\dist (5'b00110), .out(shifter_26_out));
  Shifter #(.width(32)) shifter_27 (.in(bit_extender_14_out), .\dist (5'b00101), .out(shifter_27_out));
  Shifter #(.width(32)) shifter_28 (.in(bit_extender_30_out), .\dist (5'b00100), .out(shifter_28_out));
  Shifter #(.width(32)) shifter_29 (.in(bit_extender_15_out), .\dist (5'b00011), .out(shifter_29_out));
  Shifter #(.width(32)) shifter_30 (.in(bit_extender_31_out), .\dist (5'b00010), .out(shifter_30_out));
  Shifter #(.width(32)) shifter_31 (.in(bit_extender_16_out), .\dist (5'b00001), .out(shifter_31_out));
  Shifter #(.width(32)) shifter_32 (.in(bit_extender_32_out), .\dist ({5{1'b0}}), .out(shifter_32_out));
  assign OUTPUT = shifter_1_out | shifter_2_out | shifter_3_out | shifter_4_out | shifter_5_out | shifter_6_out | shifter_7_out | shifter_8_out | shifter_9_out | shifter_10_out | shifter_11_out | shifter_12_out | shifter_13_out | shifter_14_out | shifter_15_out | shifter_16_out | shifter_17_out | shifter_18_out | shifter_19_out | shifter_20_out | shifter_21_out | shifter_22_out | shifter_23_out | shifter_24_out | shifter_25_out | shifter_26_out | shifter_27_out | shifter_28_out | shifter_29_out | shifter_30_out | shifter_31_out | shifter_32_out;  // OR_Gate or_1, 32 bits wide

  // Other names for the same wires on the sheet: Bit1[31:0] = INPUT; _5 = REVERSE_AMOUNT[0]; _4 = REVERSE_AMOUNT[1];
  //   _3 = REVERSE_AMOUNT[2]; _2 = REVERSE_AMOUNT[3]; _1 = REVERSE_AMOUNT[4]

  // Notes on the sheet:
  //   Feel free to use this component, or not, however you want!
endmodule

module u_ShiftL (
  input  [31:0] in_1,
  input  [31:0] in_2,
  output [31:0] result1
);

  wire bit_extender_2_out, bit_extender_7_out;
  wire [4:0] adder_1_out, adder_2_out, bit_extender_1_out, bit_extender_3_out, bit_extender_5_out;
  wire [31:0] bit_extender_4_out, bit_extender_6_out, demultiplexer_1_out0, demultiplexer_1_out1, result0,
       result1_t, shifter_2_out, shifter_3_out, subtractor_1_out;

  Bit_Extender #(.in_width(32), .out_width(5)) bit_extender_1 (.in(in_2), .out(bit_extender_1_out));
  Bit_Extender #(.in_width(32), .out_width(1)) bit_extender_2 (.in(in_1), .out(bit_extender_2_out));
  Shifter #(.width(32)) shifter_1 (.in(demultiplexer_1_out0), .\dist (bit_extender_1_out), .out(result0));
  Demultiplexer #(.width(32), .enable("false")) demultiplexer_1 (
    .out0(demultiplexer_1_out0), .out1(demultiplexer_1_out1), .in(in_1), .sel(bit_extender_2_out));
  Bit_Extender #(.in_width(32), .out_width(5)) bit_extender_3 (.in(in_2), .out(bit_extender_3_out));
  Adder #(.width(5)) adder_1 (.a(bit_extender_3_out), .b(5'b00001), .out(adder_1_out));  // open: cin, cout
  assign bit_extender_4_out = {{1{1'b0}}, demultiplexer_1_out1[31:1]};  // Bit_Extender bit_extender_4
  Bit_Extender #(.in_width(32), .out_width(5)) bit_extender_5 (.in(in_2), .out(bit_extender_5_out));
  assign bit_extender_6_out = {{31{1'b0}}, demultiplexer_1_out1[0]};  // Bit_Extender bit_extender_6
  Shifter #(.width(32)) shifter_2 (.in(bit_extender_6_out), .\dist (adder_1_out), .out(shifter_2_out));
  Bit_Extender #(.in_width(32), .out_width(1)) bit_extender_7 (.in(in_1), .out(bit_extender_7_out));
  Shifter #(.width(32)) shifter_3 (.in(bit_extender_4_out), .\dist (adder_2_out), .out(shifter_3_out));
  Adder #(.width(5)) adder_2 (.a(bit_extender_5_out), .b(5'b00001), .out(adder_2_out));  // open: cin, cout
  Subtractor #(.width(32)) subtractor_1 (.a(shifter_2_out), .b(32'h1), .out(subtractor_1_out));  // open: bin, bout
  Multiplexer #(.width(32), .enable("false")) multiplexer_1 (
    .in0(result0), .in1(result1_t), .out(result1), .sel(bit_extender_7_out));
  assign result1_t = shifter_3_out | subtractor_1_out;  // OR_Gate or_1, 32 bits wide

  // Other names for the same wires on the sheet: result[31:0] = result1; Source1[31:0] = in_1; Source2[31:0] = in_2
endmodule

module u_in32out16 (
  input  [31:0] data_in,
  input  \input ,
  output [15:0] upper_output,
  output [15:0] lower_output
);

  Multiplexer #(.width(16), .enable("false")) multiplexer_1 (
    .in0(data_in[31:16]), .in1(data_in[15:0]), .out(upper_output), .sel(\input ));
  Multiplexer #(.width(16), .enable("false")) multiplexer_2 (
    .in0(data_in[15:0]), .in1(data_in[31:16]), .out(lower_output), .sel(\input ));

  // Other names for the same wires on the sheet: lower[15:0] = data_in[15:0]; upper[15:0] = data_in[31:16]
endmodule

module u_in16out8 (
  input  [15:0] data_in,
  input  \input ,
  output [7:0] upper_output,
  output [7:0] lower_output
);

  Multiplexer #(.width(8), .enable("false")) multiplexer_1 (
    .in0(data_in[15:8]), .in1(data_in[7:0]), .out(upper_output), .sel(\input ));
  Multiplexer #(.width(8), .enable("false")) multiplexer_2 (
    .in0(data_in[7:0]), .in1(data_in[15:8]), .out(lower_output), .sel(\input ));

  // Other names for the same wires on the sheet: lower[7:0] = data_in[7:0]; upper[7:0] = data_in[15:8]
endmodule

module u_in8out4 (
  input  [7:0] data_in,
  input  \input ,
  output [3:0] upper_output,
  output [3:0] lower_output
);

  Multiplexer #(.width(4), .enable("false")) multiplexer_1 (
    .in0(data_in[7:4]), .in1(data_in[3:0]), .out(upper_output), .sel(\input ));
  Multiplexer #(.width(4), .enable("false")) multiplexer_2 (
    .in0(data_in[3:0]), .in1(data_in[7:4]), .out(lower_output), .sel(\input ));

  // Other names for the same wires on the sheet: lower[3:0] = data_in[3:0]; upper[3:0] = data_in[7:4]
endmodule

module u_in4out2 (
  input  [3:0] data_in,
  input  \input ,
  output [1:0] upper_output,
  output [1:0] lower_output
);

  Multiplexer #(.width(2), .enable("false")) multiplexer_1 (
    .in0(data_in[3:2]), .in1(data_in[1:0]), .out(upper_output), .sel(\input ));
  Multiplexer #(.width(2), .enable("false")) multiplexer_2 (
    .in0(data_in[1:0]), .in1(data_in[3:2]), .out(lower_output), .sel(\input ));

  // Other names for the same wires on the sheet: lower[1:0] = data_in[1:0]; upper[1:0] = data_in[3:2]
endmodule

module u_in2out1 (
  input  [1:0] data_in,
  input  \input ,
  output upper_output,
  output lower_output
);

  Multiplexer #(.enable("false")) multiplexer_1 (.in0(data_in[1]), .in1(data_in[0]), .out(upper_output), .sel(\input ));
  Multiplexer #(.enable("false")) multiplexer_2 (.in0(data_in[0]), .in1(data_in[1]), .out(lower_output), .sel(\input ));

  // Other names for the same wires on the sheet: lower = data_in[0]; upper = data_in[1]
endmodule
